# Fritzing sketch 7segment1 (saved by Fritzing 0.9.9b)
breadboards: 1

parts:
  Arduino1 = Arduino Uno (Rev3)
  S1 = Momentary Switch [package=ksa_sealed_tac_switch]
  7_Segment2 = 7 Segment Display
  R1 = Resistor [tolerance=±5% resistance=220 package="0402 [SMD]"]
  R2 = Resistor [tolerance=±5% resistance=220 package="0402 [SMD]"]

nets:
  N1: Arduino1.A3, S1.1
  N2: Arduino1.D8, 7_Segment2.Segment_A
  N3: Arduino1.D9_PWM, 7_Segment2.Segment_B
  N4: Arduino1.D2, 7_Segment2.Segment_C
  N5: Arduino1.D3_PWM, 7_Segment2.Segment_D
  N6: Arduino1.D4, 7_Segment2.Segment_E
  N7: Arduino1.D5_PWM, 7_Segment2.Segment_G
  N8: Arduino1.D6_PWM, 7_Segment2.Segment_F
  N9: Arduino1.GND, S1.4, R1.Pin_1, R2.Pin_0
  N10: 7_Segment2.common_cathode, R1.Pin_0, R2.Pin_1

// code stored in the sketch: Button.ino
int led = 3;   // PWM ? (3?? PWM ??)
int sw = 5;


boolean ledOn = false;          // LED? ?? ???? ??
boolean lastButtonState = HIGH; // ?? ?? ??


void setup() {
  pinMode(led, OUTPUT);
  pinMode(sw, INPUT_PULLUP);
  analogWrite(led, 0); // ?? ? LED ??
}


void loop() {
  boolean currentButtonState = digitalRead(sw);


  // ??? ?? ?? ?? (HIGH ? LOW)
  if (lastButtonState == HIGH && currentButtonState == LOW) {
    delay(30); // ??? ??


    if (!ledOn) {
      // LED ?? ?? ? ?? ????? ??
      for (int brightness = 0; brightness <= 255; brightness++) {
        analogWrite(led, brightness);
        delay(8);
      }
      ledOn = true;
    } else {
      // LED ?? ?? ? ?? ?????? ??
      for (int brightness = 255; brightness >= 0; brightness--) {
        analogWrite(led, brightness);
        delay(8);
      }
      ledOn = false;
    }
  }


  lastButtonState = currentButtonState;
}
