# Fritzing sketch Button_LED1 (saved by Fritzing 0.9.9b)
circuit board: 6.88566cm x 5.36311cm
breadboards: 1

parts:
  R1 = Resistor [tolerance=±5% resistance=10k power=0.25 package=THT]
  Arduino1 = Arduino Uno (Rev3)
  LED1 = LED - 5mm [color="Red (633nm)" current=0.030 package="5 mm [THT]"]
  S1 = Momentary Switch [package=ksa_sealed_tac_switch]  # not connected

nets:
  N1: R1.Pin_0, LED1.anode
  N2: R1.Pin_1, Arduino1.D3_PWM
  N3: Arduino1.GND, LED1.cathode

// code stored in the sketch: Button.ino
int led = 3; 
int sw = 5; 


boolean ledState = LOW;     // LED? ?? ?? (??/??)? ??
boolean lastButtonState = HIGH; // ?? ??? ??? ??


void setup() {
  pinMode(led, OUTPUT);
  pinMode(sw, INPUT_PULLUP);
}


void loop() {
  // ?? ??? ??? ??
  boolean currentButtonState = digitalRead(sw);


  // ??? ?? ?? (?? HIGH??? ??? ?? LOW? ?)? ??
  if (lastButtonState == HIGH && currentButtonState == LOW) {
    ledState = !ledState; // LED ??? ?? (????? ??, ????? ?)
    digitalWrite(led, ledState);
    delay(50); // ??? ?? ? ???? ???(???) ??
  }


  // ?? ??? ?? ?? ?? ??? ?? ?? ??? ??
  lastButtonState = currentButtonState;
}
