# Fritzing sketch Button_LED2 (saved by Fritzing 0.9.9b)
circuit board: 6.88566cm x 5.36311cm
breadboards: 1

parts:
  R1 = Resistor [tolerance=±5% resistance=10k power=0.25 package=THT]
  Arduino1 = Arduino Uno (Rev3)
  LED1 = LED - 5mm [color="Red (633nm)" current=0.030 package="5 mm [THT]"]
  S1 = Momentary Switch [package=ksa_sealed_tac_switch]  # not connected

nets:
  N1: R1.Pin_0, LED1.anode
  N2: R1.Pin_1, Arduino1.D3_PWM
  N3: Arduino1.GND, LED1.cathode

// code stored in the sketch: Button.ino
int led = 3;   // PWM ? (3?? PWM ??)
int sw = 5;


boolean ledOn = false;          // LED? ?? ???? ??
boolean lastButtonState = HIGH; // ?? ?? ??


void setup() {
  pinMode(led, OUTPUT);
  pinMode(sw, INPUT_PULLUP);
  analogWrite(led, 0); // ?? ? LED ??
}


void loop() {
  boolean currentButtonState = digitalRead(sw);


  // ??? ?? ?? ?? (HIGH ? LOW)
  if (lastButtonState == HIGH && currentButtonState == LOW) {
    delay(30); // ??? ??


    if (!ledOn) {
      // LED ?? ?? ? ?? ????? ??
      for (int brightness = 0; brightness <= 255; brightness++) {
        analogWrite(led, brightness);
        delay(8);
      }
      ledOn = true;
    } else {
      // LED ?? ?? ? ?? ?????? ??
      for (int brightness = 255; brightness >= 0; brightness--) {
        analogWrite(led, brightness);
        delay(8);
      }
      ledOn = false;
    }
  }


  lastButtonState = currentButtonState;
}
